// Logisim project lab.circ as structural Verilog: 1 circuit, main circuit main
module main (
  input  in_1,
  input  in_2,
  input  in_3,
  input  in_4,
  input  in_5,
  input  in_6,
  input  in_7,
  input  in_8,
  input  in_9,
  input  in_10,
  input  in_11,
  input  in_12,
  input  in_13,
  input  in_14,
  input  in_15,
  input  in_16,
  input  in_17,
  input  in_18,
  input  in_19,
  output out_20,
  output out_21,
  output out_22,
  output out_23,
  output out_24,
  output out_25,
  output out_26,
  output out_27,
  output out_28,
  output out_29
);

  wire and_1_out, and_2_out, and_3_out, not_3_out;

  not not_1 (out_20, in_3);
  nor nor_1 (out_23, in_6, in_11);
  buf buffer_1 (out_28, in_15);
  not not_2 (in_17, in_18);
  not not_3 (not_3_out, in_17);
  and and_1 (and_1_out, in_17, in_17);
  and and_2 (and_2_out, not_3_out, in_18);
  and and_3 (and_3_out, in_18, in_17, in_19);
  and and_4 (out_21, in_1, in_4);
  nand nand_1 (out_24, in_7, in_10);
  or or_1 (out_29, and_1_out, and_2_out, and_3_out);
  assign out_27 = in_16 ? ~in_14 : 1'bz;  // Controlled_Inverter controlled_inverter_1
  ExactlyOne xor_1 (.out(out_25), .in0(in_8), .in3(in_12), .in4(in_12));
  or or_2 (out_22, in_2, in_5);
  xnor xnor_1 (out_26, in_9, in_13);

  // Notes on the sheet:
  //   NOT GATE
  //   Truth table
  //   1     0
  //   0     1            
  //   NOR GATE
  //   CONTROLLED BUFFER
  //   AND GATE
  //   0     1      0
  //   1     0     0
  //   1     1     1
  //   0     0     0
  //   NAND GATE
  //   F = XY' + X'Y + XYZ
  //   CONTROLLED INVERTER
  //   XOR GATE
  //   OR GATE
  //   0     1     1
  //   1     0     1
  //   1     1     1
  //   0     0     1
  //   NAME - ADITYA GOUR
  //   ROLL NO - 330
  //   XNOR GATE
endmodule
